# Fritzing sketch MidiCircuit (saved by Fritzing 0.9.3b)
breadboards: 1

parts:
  Part1 = Arduino Mega ADK (Rev3)
  MIDI_IN = DIN-5 jack (MIDI) [package=THT]
  D1 = Rectifier Diode [part_number=1N4001 package="300 mil [THT]"]
  R1 = Resistor [tolerance=±5% resistance=220 package=THT]
  R3 = Resistor [tolerance=±5% resistance=470 package=THT]
  R4 = Resistor [tolerance=±5% resistance=10k package=THT]
  IC2 = 6n137 Optocoupler [chip_label=6n137 package="DIP (Dual Inline) [THT]"]
  MIDI_OUT = DIN-5 jack (MIDI) [package=THT]
  R5 = Resistor [tolerance=±5% resistance=220 package=THT]

nets:
  N1: Part1.D19/RX1, R3.Pin_0, IC2.Vo
  N2: Part1.D18/TX1, MIDI_OUT.5
  5V: Part1.5V, R3.Pin_1, IC2.Vcc, R5.Pin_1
  GND: Part1.GND, R4.Pin_0, IC2.GND, MIDI_OUT.2
  N3: MIDI_IN.5, D1.anode, IC2.Vf-
  N4: MIDI_IN.4, R1.Pin_1
  N5: D1.cathode, R1.Pin_0, IC2.Vf+
  N6: R4.Pin_1, IC2.Ve
  N7: MIDI_OUT.4, R5.Pin_0

notes:
  MIDI In
  MIDI Out
  Bob Kammauff
  Guardian Pipe Organ
  MIDI Connection Scematic
  470ohm Resistor can be subbed with 2x 220ohm resistors in series

custom parts:
  6n137 Optocoupler: 6n137 fast Optocoupler. With 8 pins on a 300mil dual inline package (DIP) footprint. Ve is strobe input. Output is inverting.
